# Fritzing sketch Esquema de montaje (saved by Fritzing 0.9.3b)

parts:
  Componente1 = Arduino Mega 2560 (Rev3)
  Componente2 = Analog Digital MUX Breakout
  S1 = Round Pushbutton
  S2 = Round Pushbutton
  S3 = Round Pushbutton
  S4 = Round Pushbutton
  S5 = Round Pushbutton
  S6 = Round Pushbutton
  S7 = Round Pushbutton
  Master = SPST Switch [package=switche-dpdt]
  S9 = SPST Switch [package=switche-dpdt]
  Avionica = SPST Switch [package=switche-dpdt]

nets:
  5V: Componente1.5V, Componente2.VCC
  GND: Componente1.GND, Componente2.GND, Componente2.EN, Master.O
  N1: Componente1.D22, Componente2.S0
  N2: Componente1.D23, Componente2.S1
  N3: Componente1.D24, Componente2.S2
  N4: Componente1.D25, Componente2.S3
  N5: Componente1.D38, Componente2.SIG
  N6: Componente2.C0, Master.S
  N7: Componente2.C1, S9.S
  N8: Componente2.C2, Avionica.S
  N9: Componente2.C3, S1.leg0
  N10: Componente2.C4, S2.leg0
  N11: Componente2.C5, S3.leg0
  N12: Componente2.C6, S4.leg0
  N13: Componente2.C7, S5.leg0
  N14: Componente2.C8, S6.leg0
  N15: Componente2.C9, S7.leg0

notes:
  Bomba de combustible + Iluminacion
  Master
  Avionica
